# Fritzing sketch TIC_IF_V2 (saved by Fritzing 0.9.9b)
circuit board: 2.35365cm x 3.48585cm
breadboards: 1

parts:
  R1 = Resistor [tolerance=±5% power=0.25 resistance=3300 package=THT]
  U1 = Optocoupler H11AA1 [package=THT]
  R3 = Resistor [tolerance=±5% power=0.25 resistance=1k package=THT]
  R2 = Resistor [tolerance=±5% power=0.25 resistance=10k package=THT]
  R4 = Resistor [tolerance=±5% power=0.25 resistance=330 package=THT]
  VCC = female pin header, 1 pin [form="♀ (female)"]
  GND = female pin header, 1 pin [form="♀ (female)"]
  I1 = female pin header, 1 pin [form="♀ (female)"]
  I2 = female pin header, 1 pin [form="♀ (female)"]
  C1 = Film/Foil Capacitor [part_number="330n 260V" package="15mm [THT, pp]"]
  Q1 = NPN-Transistor [part_number=2N2222 package="TO92 [THT]"]
  OUT = female pin header, 1 pin [form="♀ (female)"]

nets:
  N1: R1.Pin_0, U1.Pin_4, Q1.B
  GND: R1.Pin_1, GND.pin1, Q1.E
  N2: U1.Pin_1, R3.Pin_1
  N3: U1.Pin_2, R4.Pin_0, I2.pin1
  3.3V: U1.Pin_5, R2.Pin_0, VCC.pin1
  N4: R3.Pin_0, I1.pin1, C1.+
  N5: R2.Pin_1, Q1.C, OUT.pin1
  N6: R4.Pin_1, C1.-

custom parts:
  Optocoupler H11AA1: Double polarity Optocoupler
  Film/Foil Capacitor: Polypropylene/Film and Foil capacitor.
